// Logisim project new.circ as structural Verilog: 1 circuit, main circuit main
module main (
);

  wire and_1_out, cdm_16_1_p1, cdm_16_1_p2, cdm_16_1_p3, cdm_16_1_p7, cdm_16_1_p8, cdm_16_1_p9, cdm_16_1_p10,
       cdm_16_1_p11, Cl, comparator_1_eq, comparator_2_gt, comparator_3_lt, decoder_1_out0, decoder_1_out1,
       decoder_1_out2, decoder_1_out3, decoder_1_out4, decoder_1_out5, decoder_1_out6, decoder_1_out7,
       decoder_1_out8, decoder_1_out9, decoder_1_out10, decoder_1_out11, decoder_1_out12, decoder_1_out13,
       decoder_1_out14, decoder_1_out15, Display_sel, DOWN_button, LEFT_button, mem, not_1_out, not_2_out,
       not_3_out, read, RIGHT_button, UP_button, word;
  wire [3:3] not_4_out;
  wire [15:0] address_bus, cdm_16_1_p16, cdm_16_1_p17, D, PROGRESS, register_1_q, register_2_q, register_3_q,
       register_4_q, register_5_q, register_6_q, register_8_q, register_9_q, register_10_q, register_11_q,
       register_12_q, register_13_q, register_14_q, register_15_q, register_16_q, register_17_q;

  // Probe on cdm_16_1_p8
  // Probe on cdm_16_1_p7
  // Probe on cdm_16_1_p9
  // CdM_16 cdm_16_1: pin names not known; wires that end beside it: cdm_16_1_p1, cdm_16_1_p2, cdm_16_1_p3, cdm_16_1_p1, cdm_16_1_p2, cdm_16_1_p3, cdm_16_1_p7, cdm_16_1_p8, cdm_16_1_p9, cdm_16_1_p10, cdm_16_1_p11, mem, read, word, address_bus, cdm_16_1_p16, cdm_16_1_p17
  Clock clock_1 (.out(Cl));
  // Debugger debugger_1: pin names not known; wires that end beside it: Cl
  // Probe on cdm_16_1_p10
  // Probe on cdm_16_1_p11
  Button LEFT (.out(LEFT_button));
  assign D = not_1_out ? cdm_16_1_p16 : 16'bz;  // Controlled_Buffer controlled_buffer_1
  not not_1 (not_1_out, read);
  assign cdm_16_1_p17 = read ? D : 16'bz;  // Controlled_Buffer controlled_buffer_2
  Button UP (.out(UP_button));
  Button RIGHT (.out(RIGHT_button));
  Button DOWN (.out(DOWN_button));
  Register #(.width(16)) register_1 (.D(D), .Q(register_1_q), .clk(decoder_1_out0));  // open: en, clr
  Register #(.width(16)) register_2 (.D(D), .Q(register_2_q), .clk(decoder_1_out1));  // open: en, clr
  Register #(.width(16)) register_3 (.D(D), .Q(register_3_q), .clk(decoder_1_out2));  // open: en, clr
  Register #(.width(16)) register_4 (.D(D), .Q(register_4_q), .clk(decoder_1_out3));  // open: en, clr
  Comparator #(.width(16)) comparator_1 (.a(address_bus), .b(16'hffc0), .eq(comparator_1_eq));  // open: gt, lt
  // RAM ram_1: pin names not known; wires that end beside it: address_bus, word, mem, Cl, read, D
  Register #(.width(16)) register_5 (.D(D), .Q(register_5_q), .clk(decoder_1_out5));  // open: en, clr
  Register #(.width(16)) register_6 (.D(D), .Q(register_6_q), .clk(decoder_1_out4));  // open: en, clr
  Register #(.width(16)) register_7 (.D(D), .Q(PROGRESS), .clk(and_1_out));  // open: en, clr
  not not_2 (not_2_out, read);
  and and_1 (and_1_out, not_2_out, mem, comparator_1_eq);
  DotMatrix #(.inputtype("row"), .matrixcols(16), .matrixrows(1)) dotmatrix_1 (.row0(PROGRESS));
  DotMatrix #(.matrixcols(16), .matrixrows(16)) dotmatrix_2 (
    .col0(register_1_q), .col1(register_2_q), .col2(register_3_q), .col3(register_4_q), .col4(register_6_q),
    .col5(register_5_q), .col6(register_8_q), .col7(register_10_q), .col8(register_9_q),
    .col9(register_11_q), .col10(register_12_q), .col11(register_13_q), .col12(register_15_q),
    .col13(register_14_q), .col14(register_16_q), .col15(register_17_q));
  Register #(.width(16)) register_8 (.D(D), .Q(register_8_q), .clk(decoder_1_out6));  // open: en, clr
  Register #(.width(16)) register_9 (.D(D), .Q(register_9_q), .clk(decoder_1_out8));  // open: en, clr
  Register #(.width(16)) register_10 (.D(D), .Q(register_10_q), .clk(decoder_1_out7));  // open: en, clr
  Register #(.width(16)) register_11 (.D(D), .Q(register_11_q), .clk(decoder_1_out9));  // open: en, clr
  Register #(.width(16)) register_12 (.D(D), .Q(register_12_q), .clk(decoder_1_out10));  // open: en, clr
  Decoder #(.select(4), .disabled(0)) decoder_1 (
    .out0(decoder_1_out0), .out1(decoder_1_out1), .out2(decoder_1_out2), .out3(decoder_1_out3),
    .out4(decoder_1_out4), .out5(decoder_1_out5), .out6(decoder_1_out6), .out7(decoder_1_out7),
    .out8(decoder_1_out8), .out9(decoder_1_out9), .out10(decoder_1_out10), .out11(decoder_1_out11),
    .out12(decoder_1_out12), .out13(decoder_1_out13), .out14(decoder_1_out14), .out15(decoder_1_out15),
    .sel({not_4_out[3], address_bus[3:1]}), .en(Display_sel));
  not not_3 (not_3_out, read);
  Comparator #(.width(16), .mode("unsigned")) comparator_2 (
    .a(address_bus), .b(16'hffcf), .gt(comparator_2_gt));  // open: eq, lt
  Comparator #(.width(16), .mode("unsigned")) comparator_3 (
    .a(address_bus), .b(16'hfff0), .lt(comparator_3_lt));  // open: gt, eq
  Register #(.width(16)) register_13 (.D(D), .Q(register_13_q), .clk(decoder_1_out11));  // open: en, clr
  and and_2 (Display_sel, not_3_out, mem, comparator_2_gt, comparator_3_lt);
  Register #(.width(16)) register_14 (.D(D), .Q(register_14_q), .clk(decoder_1_out13));  // open: en, clr
  Register #(.width(16)) register_15 (.D(D), .Q(register_15_q), .clk(decoder_1_out12));  // open: en, clr
  Register #(.width(16)) register_16 (.D(D), .Q(register_16_q), .clk(decoder_1_out14));  // open: en, clr
  not not_4 (not_4_out[3], address_bus[4]);
  Register #(.width(16)) register_17 (.D(D), .Q(register_17_q), .clk(decoder_1_out15));  // open: en, clr

  // Other names for the same wires on the sheet: data_bus[15:0] = D
endmodule
